// Logisim project adder.circ as structural Verilog
module main (
  input  [15:0] A,
  input  [15:0] B,
  input  sub,
  output C,
  output [15:0] result
);

  wire eighbitcircuit_1_cout, fourbitadder_1_cout, onebitadder_1_cout, twobitcircuit_1_cout;
  wire [15:0] binput_1_out_3;

  binput binput_1 (.b(B), .c(sub), .out_3(binput_1_out_3));
  eighbitcircuit eighbitcircuit_1 (
    .a(A[7:0]), .b(binput_1_out_3[7:0]), .CIn(sub), .s(result[7:0]), .COut(eighbitcircuit_1_cout));
  fourbitadder fourbitadder_1 (
    .a(A[11:8]), .b(binput_1_out_3[11:8]), .CIn(eighbitcircuit_1_cout), .s(result[11:8]),
    .COut(fourbitadder_1_cout));
  twobitcircuit twobitcircuit_1 (
    .a(A[13:12]), .b(binput_1_out_3[13:12]), .Cin(fourbitadder_1_cout), .s(result[13:12]),
    .COut(twobitcircuit_1_cout));
  onebitadder onebitadder_1 (
    .a(A[14]), .b(binput_1_out_3[14]), .cIn(twobitcircuit_1_cout), .s(result[14]), .COut(onebitadder_1_cout));
  onebitadder onebitadder_2 (.a(A[15]), .b(binput_1_out_3[15]), .cIn(onebitadder_1_cout), .s(result[15]), .COut(C));

  // Other names for the same wires on the sheet: sum[15:0] = result
endmodule

module onebitadder (
  input  a,
  input  b,
  input  cIn,
  output s,
  output COut
);

  wire and_1_out, and_2_out, and_3_out, and_4_out, xor_1_out, xor_2_out;

  and and_1 (and_1_out, a, cIn);
  and and_2 (and_2_out, a, b);
  and and_3 (and_3_out, b, cIn);
  and and_4 (and_4_out, a, a, b, cIn);
  xor xor_1 (xor_1_out, a, b);
  or or_1 (COut, and_1_out, and_2_out, and_3_out);
  xor xor_2 (xor_2_out, xor_1_out, cIn);
  or or_2 (s, and_4_out, xor_2_out);
endmodule

module twobitcircuit (
  input  [1:0] a,
  input  [1:0] b,
  input  Cin,
  output [1:0] s,
  output COut
);

  wire onebitadder_1_cout;

  onebitadder onebitadder_1 (.a(a[0]), .b(b[0]), .cIn(Cin), .s(s[0]), .COut(onebitadder_1_cout));
  onebitadder onebitadder_2 (.a(a[1]), .b(b[1]), .cIn(onebitadder_1_cout), .s(s[1]), .COut(COut));
endmodule

module fourbitadder (
  input  [3:0] a,
  input  [3:0] b,
  input  CIn,
  output [3:0] s,
  output COut
);

  wire twobitcircuit_1_cout;

  twobitcircuit twobitcircuit_1 (.a(a[1:0]), .b(b[1:0]), .Cin(CIn), .s(s[1:0]), .COut(twobitcircuit_1_cout));
  twobitcircuit twobitcircuit_2 (.a(a[3:2]), .b(b[3:2]), .Cin(twobitcircuit_1_cout), .s(s[3:2]), .COut(COut));
endmodule

module eighbitcircuit (
  input  [7:0] a,
  input  [7:0] b,
  input  CIn,
  output [7:0] s,
  output COut
);

  wire fourbitadder_1_cout;

  fourbitadder fourbitadder_1 (.a(a[3:0]), .b(b[3:0]), .CIn(CIn), .s(s[3:0]), .COut(fourbitadder_1_cout));
  fourbitadder fourbitadder_2 (.a(a[7:4]), .b(b[7:4]), .CIn(fourbitadder_1_cout), .s(s[7:4]), .COut(COut));
endmodule

module binput (
  input  [15:0] b,
  input  c,
  output [15:0] out_3
);

  xor xor_1 (out_3[0], b[0], c);
  xor xor_2 (out_3[1], b[1], c);
  xor xor_3 (out_3[2], b[2], c);
  xor xor_4 (out_3[3], b[3], c);
  xor xor_5 (out_3[4], b[4], c);
  xor xor_6 (out_3[5], b[5], c);
  xor xor_7 (out_3[6], b[6], c);
  xor xor_8 (out_3[7], b[7], c);
  xor xor_9 (out_3[8], b[8], c);
  xor xor_10 (out_3[9], b[9], c);
  xor xor_11 (out_3[10], b[10], c);
  xor xor_12 (out_3[11], c, b[11]);
  xor xor_13 (out_3[12], b[12], c);
  xor xor_14 (out_3[13], b[13], c);
  xor xor_15 (out_3[14], b[14], c);
  xor xor_16 (out_3[15], b[15], c);
endmodule
